// Logisim project Processor.circ as structural Verilog: 4 circuits, main circuit main
module main (
);

  ULA ula_1 ();  // open: F2, F1, F0, A, B, C
  Datapath datapath_1 ();  // open: Ext__Data_MBR, in_2, in_3, in_4, in_5, in_6, Reset, in_9, in_10, in_11, External_Input, in_12, B_Bus_Selector, Output, Clock, Ext__Addr_MBR
endmodule

module ULA (
  input  [7:0] A,
  input  F2,
  input  F1,
  input  F0,
  input  [7:0] B,
  output [7:0] C
);

  wire [7:0] adder_1_out, adder_2_out, adder_3_out, and_1_out, or_1_out, subtractor_1_out;

  Adder adder_1 (.a(A), .b(8'h1), .out(adder_1_out));  // open: cin, cout
  Adder adder_2 (.a(B), .b(8'h1), .out(adder_2_out));  // open: cin, cout
  Adder adder_3 (.a(A), .b(B), .out(adder_3_out));  // open: cin, cout
  Subtractor subtractor_1 (.a(A), .b(B), .out(subtractor_1_out));  // open: bin, bout
  assign and_1_out = A & B;  // AND_Gate and_1, 8 bits wide
  assign or_1_out = A | B;  // OR_Gate or_1, 8 bits wide
  Multiplexer #(.select(3), .width(8)) multiplexer_1 (
    .in0(A), .in1(B), .in2(adder_1_out), .in3(adder_2_out), .in4(adder_3_out), .in5(subtractor_1_out),
    .in6(and_1_out), .in7(or_1_out), .out(C), .sel({F2, F1, F0}));  // open: en
endmodule

module Datapath (
  input  [7:0] Ext__Data_MBR,
  input  in_2,
  input  in_3,
  input  in_4,
  input  in_5,
  input  in_6,
  input  Reset,
  input  Clock,
  input  in_9,
  input  in_10,
  input  in_11,
  input  in_12,
  input  B_Bus_Selector,
  input  [7:0] External_Input,
  output [7:0] Ext__Addr_MBR,
  output [7:0] Output
);

  wire [7:0] A_q, B_q, MBR_q, multiplexer_1_out, ula_1_c;

  Register A (.D(ula_1_c), .en(in_6), .Q(A_q), .clk(Clock), .clr(Reset));
  Register B (.D(ula_1_c), .en(in_5), .Q(B_q), .clk(Clock), .clr(Reset));
  Register MBR (.D(Ext__Data_MBR), .en(in_4), .Q(MBR_q), .clk(Clock), .clr(Reset));
  Register PC (.D(ula_1_c), .en(in_3), .Q(Ext__Addr_MBR), .clk(Clock), .clr(Reset));
  Register OUT (.D(ula_1_c), .en(in_2), .Q(Output), .clk(Clock), .clr(Reset));
  Multiplexer #(.select(2), .width(8)) multiplexer_1 (
    .in0(B_q), .in1(MBR_q), .in2(Ext__Addr_MBR), .in3(External_Input), .out(multiplexer_1_out),
    .sel({in_12, B_Bus_Selector}), .en(1'b1));
  ULA ula_1 (.F2(in_9), .F1(in_10), .F0(in_11), .A(A_q), .B(multiplexer_1_out), .C(ula_1_c));
endmodule

module Control_Unit (
  input  [7:0] Input,
  input  Clear,
  input  [7:0] External_Data_M__Bus,
  output [7:0] Output,
  output [7:0] External_Addr_M__Bus
);

  wire clock_1_out;
  wire [4:0] bit_extender_1_out, MIR_q_2, MPC_q, multiplexer_1_out;
  wire [10:0] MIR_q;
  wire [15:0] rom_1_data;

  Clock clock_1 (.out(clock_1_out));
  Datapath datapath_1 (
    .Ext__Data_MBR(External_Data_M__Bus), .in_2(MIR_q[6]), .in_3(MIR_q[5]), .in_4(MIR_q[4]), .in_5(MIR_q[3]),
    .in_6(MIR_q[2]), .Reset(Clear), .in_9(MIR_q[9]), .in_10(MIR_q[8]), .in_11(MIR_q[7]),
    .External_Input(Input), .in_12(MIR_q[1]), .B_Bus_Selector(MIR_q[0]), .Output(Output),
    .Clock(clock_1_out), .Ext__Addr_MBR(External_Addr_M__Bus));
  Bit_Extender #(.out_width(5)) bit_extender_1 (.in(Output), .out(bit_extender_1_out));
  Multiplexer #(.width(5)) multiplexer_1 (
    .in0(bit_extender_1_out), .in1(MIR_q_2), .out(multiplexer_1_out), .sel(MIR_q[10]));  // open: en
  Register #(.width(5)) MPC (.D(multiplexer_1_out), .Q(MPC_q), .clk(clock_1_out), .clr(Clear));  // open: en
  ROM #(.addrWidth(5), .dataWidth(16)) rom_1 (.addr(MPC_q), .data(rom_1_data));  // open: sel
  Register #(.width(16), .trigger("falling")) MIR (
    .D(rom_1_data), .Q({MIR_q_2, MIR_q}), .clk(clock_1_out), .clr(Clear));  // open: en

  // Notes on the sheet:
  //   contents of rom_1 (hex, n*v repeats v):
  //   e40 2
endmodule
